// Logisim project Most Final Circuit.circ as structural Verilog: 6 circuits, main circuit main
module main (
  input  Add_Sub,
  input  Compareter,
  input  A3,
  input  A2,
  input  A1,
  input  A0,
  input  B3,
  input  B2,
  input  B1,
  input  B0,
  output Equal,
  output Greater,
  output Smaller
);

  wire and_2_out, and_4_out, and_5_out, and_6_out, full_adder_4x1_mux_1n_1_carry,
       full_adder_4x1_mux_1n_1_sum, full_adder_4x1_mux_1n_2_carry, full_adder_4x1_mux_1n_2_sum,
       full_adder_4x1_mux_1n_3_carry, full_adder_4x1_mux_1n_3_sum, full_adder_4x1_mux_1n_4_carry,
       full_adder_4x1_mux_1n_4_sum, l_7_segment_display_driver_4807627b_1_p5,
       l_7_segment_display_driver_4807627b_1_p6, l_7_segment_display_driver_4807627b_1_p7,
       l_7_segment_display_driver_4807627b_1_p8, l_7_segment_display_driver_4807627b_1_p9,
       l_7_segment_display_driver_4807627b_1_p10, l_7_segment_display_driver_4807627b_1_p11, n74153_1_pin1,
       n74153_1_pin2, n74153_1_pin9, n74153_1_pin15, n74283_1_pin1, n74283_1_pin2, n74283_1_pin4,
       n74283_1_pin6, n74283_1_pin9, n74283_1_pin10, n74283_1_pin11, n74283_1_pin13, not_3_out, or_1_out,
       or_2_out, or_3_out, or_4_out, or_5_out, or_6_out, signed_converter_2_1_r0, signed_converter_2_1_r1,
       signed_converter_2_1_r2, signed_converter_2_1_r3, signed_converter_2_2_r0, signed_converter_2_2_r1,
       signed_converter_2_2_r2, signed_converter_2_2_r3, undriven, xor_1_out, xor_2_out, xor_3_out,
       xor_4_out, xor_6_out, xor_7_out, xor_8_out, xor_9_out;

  signed_converter_2 signed_converter_2_1 (
    .A3(A3), .A2(A2), .A1(A1), .A0(A0), .R3(signed_converter_2_1_r3), .R2(signed_converter_2_1_r2),
    .R1(signed_converter_2_1_r1), .R0(signed_converter_2_1_r0));
  signed_converter_2 signed_converter_2_2 (
    .A3(B3), .A2(B2), .A1(B1), .A0(B0), .R3(signed_converter_2_2_r3), .R2(signed_converter_2_2_r2),
    .R1(signed_converter_2_2_r1), .R0(signed_converter_2_2_r0));
  xor xor_1 (xor_1_out, signed_converter_2_2_r3, n74153_1_pin9);
  xor xor_2 (xor_2_out, signed_converter_2_2_r2, n74153_1_pin9);
  xor xor_3 (xor_3_out, signed_converter_2_2_r1, n74153_1_pin9);
  xor xor_4 (xor_4_out, signed_converter_2_2_r0, n74153_1_pin9);
  Full_Adder_4x1_MUX_1N full_adder_4x1_mux_1n_1 (
    .A0(signed_converter_2_1_r3), .B0(xor_1_out), .Cin(full_adder_4x1_mux_1n_2_carry),
    .CARRY(full_adder_4x1_mux_1n_1_carry), .SUM(full_adder_4x1_mux_1n_1_sum));
  Full_Adder_4x1_MUX_1N full_adder_4x1_mux_1n_2 (
    .A0(signed_converter_2_1_r2), .B0(xor_2_out), .Cin(full_adder_4x1_mux_1n_3_carry),
    .CARRY(full_adder_4x1_mux_1n_2_carry), .SUM(full_adder_4x1_mux_1n_2_sum));
  Full_Adder_4x1_MUX_1N full_adder_4x1_mux_1n_3 (
    .A0(signed_converter_2_1_r1), .B0(xor_3_out), .Cin(full_adder_4x1_mux_1n_4_carry),
    .CARRY(full_adder_4x1_mux_1n_3_carry), .SUM(full_adder_4x1_mux_1n_3_sum));
  Full_Adder_4x1_MUX_1N full_adder_4x1_mux_1n_4 (
    .A0(signed_converter_2_1_r0), .B0(xor_4_out), .Cin(n74153_1_pin9), .CARRY(full_adder_4x1_mux_1n_4_carry),
    .SUM(full_adder_4x1_mux_1n_4_sum));
  _74153 u_74153_1 (
    .pin1(n74153_1_pin1), .pin2(n74153_1_pin2), .pin3(full_adder_4x1_mux_1n_1_carry),
    .pin4(full_adder_4x1_mux_1n_1_carry), .pin5(full_adder_4x1_mux_1n_1_sum),
    .pin6(full_adder_4x1_mux_1n_1_sum), .pin7(Smaller), .pin15(n74153_1_pin15), .pin14(Compareter),
    .pin13(Compareter), .pin12(Add_Sub), .pin11(Compareter), .pin10(Add_Sub), .pin9(n74153_1_pin9));
  xor xor_5 (n74153_1_pin2, full_adder_4x1_mux_1n_1_carry, full_adder_4x1_mux_1n_2_carry);
  xor xor_6 (xor_6_out, Smaller, full_adder_4x1_mux_1n_1_sum);
  xor xor_7 (xor_7_out, Smaller, full_adder_4x1_mux_1n_2_sum);
  xor xor_8 (xor_8_out, Smaller, full_adder_4x1_mux_1n_3_sum);
  xor xor_9 (xor_9_out, Smaller, full_adder_4x1_mux_1n_4_sum);
  or or_1 (or_1_out, Equal, Smaller);
  not not_1 (Greater, or_1_out);
  _74283 u_74283_1 (
    .pin1(n74283_1_pin1), .pin2(n74283_1_pin2), .pin3(xor_8_out), .pin4(n74283_1_pin4), .pin5(xor_9_out),
    .pin6(n74283_1_pin6), .pin7(Smaller), .pin15(n74283_1_pin2), .pin14(xor_7_out), .pin13(n74283_1_pin13),
    .pin12(xor_6_out), .pin11(n74283_1_pin11), .pin10(n74283_1_pin10), .pin9(n74283_1_pin9));
  or or_2 (or_2_out, full_adder_4x1_mux_1n_3_sum, full_adder_4x1_mux_1n_4_sum);
  and and_1 (n74283_1_pin2, xor_6_out, or_3_out);
  or or_3 (or_3_out, full_adder_4x1_mux_1n_2_sum, or_2_out);
  or or_4 (or_4_out, full_adder_4x1_mux_1n_1_sum, or_3_out);
  // OR_Gate or_5 has open pins: out=or_5_out
  not not_2 (Equal, or_4_out);
  not not_3 (not_3_out, undriven);
  buf and_2 (and_2_out, or_5_out);  // AND_Gate
  // AND_Gate and_3 has open pins: in0=not_3_out, in1=and_2_out, out=open
  and and_4 (and_4_out, Compareter, Greater);
  and and_5 (and_5_out, Compareter, Equal);
  and and_6 (and_6_out, Compareter, Smaller);
  // L_7_segment_display_driver_4807627b l_7_segment_display_driver_4807627b_1: pin names not known; wires that end beside it: n74283_1_pin10, n74283_1_pin13, n74283_1_pin1, n74283_1_pin4, l_7_segment_display_driver_4807627b_1_p5, l_7_segment_display_driver_4807627b_1_p6, l_7_segment_display_driver_4807627b_1_p7, l_7_segment_display_driver_4807627b_1_p8, l_7_segment_display_driver_4807627b_1_p9, l_7_segment_display_driver_4807627b_1_p10, l_7_segment_display_driver_4807627b_1_p11
  or or_6 (or_6_out, and_6_out, Smaller);
  _7_Segment_Display u_7_segment_display_1 (
    .g(and_5_out), .a(and_5_out), .b(and_4_out), .d(or_6_out), .c(and_4_out));  // open: f, e, dp
  _7_Segment_Display u_7_segment_display_2 (.b(n74283_1_pin9), .c(n74283_1_pin9));  // open: g, f, a, e, d, dp
  _7_Segment_Display u_7_segment_display_3 (
    .g(l_7_segment_display_driver_4807627b_1_p11), .f(l_7_segment_display_driver_4807627b_1_p10),
    .a(l_7_segment_display_driver_4807627b_1_p5), .b(l_7_segment_display_driver_4807627b_1_p6),
    .e(l_7_segment_display_driver_4807627b_1_p9), .d(l_7_segment_display_driver_4807627b_1_p8),
    .c(l_7_segment_display_driver_4807627b_1_p7));  // open: dp
  // also tied to GND on the sheet: {n74153_1_pin1, n74153_1_pin15, n74283_1_pin11, n74283_1_pin6}
endmodule

module Full_Adder_4x1_MUX_1N (
  input  A0,
  input  B0,
  input  Cin,
  output CARRY,
  output SUM
);

  wire n74153_1_pin1, n74153_1_pin4, n74153_1_pin13, n74153_1_pin15;

  _74153 u_74153_1 (
    .pin1(n74153_1_pin1), .pin2(A0), .pin3(B0), .pin4(n74153_1_pin4), .pin5(n74153_1_pin4), .pin6(B0),
    .pin7(SUM), .pin15(n74153_1_pin15), .pin14(Cin), .pin13(n74153_1_pin13), .pin12(B0), .pin11(B0),
    .pin10(n74153_1_pin15), .pin9(CARRY));
  not not_1 (n74153_1_pin4, B0);
  // also tied to GND on the sheet: {n74153_1_pin1, n74153_1_pin15}
  // also tied to VCC on the sheet: n74153_1_pin13
endmodule

module Signed_Converter (
  input  A0,
  input  A1,
  input  A2,
  input  A3,
  output R0,
  output R1,
  output R2,
  output R3
);

  wire n74138_1_pin4, n74138_1_pin5, n74138_1_pin7, n74138_1_pin9, n74138_1_pin10, n74138_1_pin11,
       n74138_1_pin12, n74138_1_pin13, n74138_1_pin14, n74138_1_pin15, n74138_2_pin4, n74138_2_pin5,
       n74138_2_pin7, n74138_2_pin9, n74138_2_pin10, n74138_2_pin11, n74138_2_pin12, n74138_2_pin13,
       n74138_2_pin14, n74138_2_pin15, not_1_out, not_5_out, not_6_out, not_7_out, not_8_out, not_9_out,
       not_10_out, not_11_out, not_12_out, not_13_out, not_14_out, not_15_out, not_16_out, not_17_out,
       or_1_out, or_2_out, or_3_out, or_5_out, or_6_out, or_8_out;

  not not_1 (not_1_out, A0);
  // NOT_Gate not_2 has open pins: in=n74138_1_pin15, out=open
  _74138 u_74138_1 (
    .pin1(A3), .pin2(A2), .pin3(A1), .pin4(n74138_1_pin4), .pin5(n74138_1_pin5), .pin6(not_1_out),
    .pin7(n74138_1_pin7), .pin15(n74138_1_pin15), .pin14(n74138_1_pin14), .pin13(n74138_1_pin13),
    .pin12(n74138_1_pin12), .pin11(n74138_1_pin11), .pin10(n74138_1_pin10), .pin9(n74138_1_pin9));
  // NOT_Gate not_3 has open pins: in=n74138_2_pin15, out=open
  _74138 u_74138_2 (
    .pin1(A3), .pin2(A2), .pin3(A1), .pin4(n74138_2_pin4), .pin5(n74138_2_pin5), .pin6(A0),
    .pin7(n74138_2_pin7), .pin15(n74138_2_pin15), .pin14(n74138_2_pin14), .pin13(n74138_2_pin13),
    .pin12(n74138_2_pin12), .pin11(n74138_2_pin11), .pin10(n74138_2_pin10), .pin9(n74138_2_pin9));
  // NOT_Gate not_4 has open pins: in=n74138_1_pin14, out=open
  not not_5 (not_5_out, n74138_1_pin13);
  not not_6 (not_6_out, n74138_1_pin12);
  not not_7 (not_7_out, n74138_1_pin11);
  not not_8 (not_8_out, n74138_2_pin14);
  not not_9 (not_9_out, n74138_2_pin13);
  not not_10 (not_10_out, n74138_2_pin12);
  not not_11 (not_11_out, n74138_2_pin11);
  not not_12 (not_12_out, n74138_1_pin10);
  not not_13 (not_13_out, n74138_1_pin9);
  not not_14 (not_14_out, n74138_1_pin7);
  not not_15 (not_15_out, n74138_2_pin10);
  not not_16 (not_16_out, n74138_2_pin9);
  not not_17 (not_17_out, n74138_2_pin7);
  or or_1 (or_1_out, not_5_out, not_6_out, not_13_out, not_14_out);
  or or_2 (or_2_out, not_7_out, not_12_out, not_13_out, not_14_out);
  or or_3 (or_3_out, or_1_out, not_8_out, not_9_out, not_15_out);
  or or_4 (R2, or_3_out, not_16_out);
  or or_5 (or_5_out, or_2_out, not_8_out, not_9_out, not_10_out);
  or or_6 (or_6_out, not_8_out, not_9_out, not_10_out, not_15_out);
  or or_7 (R1, or_5_out, not_15_out);
  or or_8 (or_8_out, or_6_out, not_16_out);
  or or_9 (R0, or_8_out, not_17_out);

  assign R3 = A3;
  // also tied to GND on the sheet: {n74138_1_pin4, n74138_2_pin4, n74138_1_pin5, n74138_2_pin5}
endmodule

module binary_To_BCD (
  input  C3,
  input  C2,
  input  C1,
  input  C0
);

  _74153 u_74153_1 ();  // open: pin1, pin2, pin3, pin4, pin5, pin6, pin7, pin15, pin14, pin13, pin12, pin11, pin10, pin9
endmodule

module Full_4_Bit_Adder (
  input  in_1,
  input  in_2,
  input  in_3,
  input  in_4,
  input  A3,
  input  B3,
  input  A2,
  input  B2,
  input  A1,
  input  B1,
  input  A0,
  input  B0,
  input  Add_Sub,
  output SIGN
);

  wire full_adder_4x1_mux_1n_1_carry, full_adder_4x1_mux_1n_1_sum, full_adder_4x1_mux_1n_2_carry,
       full_adder_4x1_mux_1n_2_sum, full_adder_4x1_mux_1n_3_carry, full_adder_4x1_mux_1n_3_sum,
       full_adder_4x1_mux_1n_4_carry, full_adder_4x1_mux_1n_4_sum, n74157_1_pin15, xor_1_out, xor_2_out,
       xor_3_out, xor_4_out, xor_5_out;

  xor xor_1 (xor_1_out, B3, Add_Sub);
  xor xor_2 (xor_2_out, B2, Add_Sub);
  xor xor_3 (xor_3_out, B1, Add_Sub);
  xor xor_4 (xor_4_out, B0, Add_Sub);
  Full_Adder_4x1_MUX_1N full_adder_4x1_mux_1n_1 (
    .A0(A3), .B0(xor_1_out), .Cin(full_adder_4x1_mux_1n_2_carry), .CARRY(full_adder_4x1_mux_1n_1_carry),
    .SUM(full_adder_4x1_mux_1n_1_sum));
  Full_Adder_4x1_MUX_1N full_adder_4x1_mux_1n_2 (
    .A0(A2), .B0(xor_2_out), .Cin(full_adder_4x1_mux_1n_3_carry), .CARRY(full_adder_4x1_mux_1n_2_carry),
    .SUM(full_adder_4x1_mux_1n_2_sum));
  Full_Adder_4x1_MUX_1N full_adder_4x1_mux_1n_3 (
    .A0(A1), .B0(xor_3_out), .Cin(full_adder_4x1_mux_1n_4_carry), .CARRY(full_adder_4x1_mux_1n_3_carry),
    .SUM(full_adder_4x1_mux_1n_3_sum));
  Full_Adder_4x1_MUX_1N full_adder_4x1_mux_1n_4 (
    .A0(A0), .B0(xor_4_out), .Cin(Add_Sub), .CARRY(full_adder_4x1_mux_1n_4_carry),
    .SUM(full_adder_4x1_mux_1n_4_sum));
  xor xor_5 (xor_5_out, full_adder_4x1_mux_1n_1_carry, full_adder_4x1_mux_1n_2_carry);
  _74157 u_74157_1 (
    .pin1(xor_5_out), .pin2(full_adder_4x1_mux_1n_1_sum), .pin3(full_adder_4x1_mux_1n_1_carry), .pin4(SIGN),
    .pin15(n74157_1_pin15));  // open: pin5, pin6, pin7, pin14, pin13, pin12, pin11, pin10, pin9
  // XOR_Gate xor_6 has open pins: in0=SIGN, in1=full_adder_4x1_mux_1n_1_sum, out=open
  // XOR_Gate xor_7 has open pins: in0=SIGN, in1=full_adder_4x1_mux_1n_2_sum, out=open
  // XOR_Gate xor_8 has open pins: in0=SIGN, in1=full_adder_4x1_mux_1n_3_sum, out=open
  // XOR_Gate xor_9 has open pins: in0=SIGN, in1=full_adder_4x1_mux_1n_4_sum, out=open
  _74283 u_74283_1 (.pin7(SIGN));  // open: pin1, pin2, pin3, pin4, pin5, pin6, pin15, pin14, pin13, pin12, pin11, pin10, pin9
  // also tied to GND on the sheet: n74157_1_pin15

  // Notes on the sheet:
  //   Not Complete
  //   Still in signed complement form
endmodule

module signed_converter_2 (
  input  A3,
  input  A2,
  input  A1,
  input  A0,
  output R3,
  output R2,
  output R1,
  output R0
);

  wire n74283_1_pin2, n74283_1_pin6, n74283_1_pin11, n74283_1_pin15, xor_1_out, xor_2_out, xor_3_out;

  xor xor_1 (xor_1_out, A2, A3);
  xor xor_2 (xor_2_out, A1, A3);
  xor xor_3 (xor_3_out, A0, A3);
  _74283 u_74283_1 (
    .pin1(R1), .pin2(n74283_1_pin2), .pin3(xor_2_out), .pin4(R0), .pin5(xor_3_out), .pin6(n74283_1_pin6),
    .pin7(A3), .pin15(n74283_1_pin15), .pin14(xor_1_out), .pin13(R2), .pin12(A3), .pin11(n74283_1_pin11),
    .pin10(R3));  // open: pin9
  // also tied to GND on the sheet: {n74283_1_pin15, n74283_1_pin2, n74283_1_pin11, n74283_1_pin6}
endmodule
